// Digital circuit main.dig as structural Verilog
module main (
  output out_1,
  output out_2
);

  // And and_1 has open pins: In_1=out_1, In_2=out_1, out=open
  Button button_1 (.out(out_1));
  LED led_1 (.in(out_1));

  assign out_2 = out_1;
endmodule
